// Logisim project cpu.circ as structural Verilog: 8 circuits, main circuit CPU
module ULA (
  input  [7:0] ULA_SOURCE_2,
  input  [7:0] ULA_SOURCE_1,
  input  [2:0] ULA_OPCODE,
  output [7:0] ULA_OUT,
  output ULA_CARRY,
  output ULA_UNSIGNED_GREATER,
  output ULA_SIGNED_GREATER,
  output ULA_EQUAL
);

  wire [7:0] adder_1_out, and_1_out, or_1_out, shifter_1_out, shifter_2_out;

  assign and_1_out = ULA_SOURCE_1 & ULA_SOURCE_2;  // AND_Gate and_1, 8 bits wide
  assign or_1_out = ULA_SOURCE_1 | ULA_SOURCE_2;  // OR_Gate or_1, 8 bits wide
  Adder adder_1 (.a(ULA_SOURCE_1), .b(ULA_SOURCE_2), .out(adder_1_out), .cin(1'b0), .cout(ULA_CARRY));
  Shifter shifter_1 (.in(ULA_SOURCE_2), .\dist (ULA_SOURCE_1[2:0]), .out(shifter_1_out));
  Shifter #(.shift("lr")) shifter_2 (.in(ULA_SOURCE_2), .\dist (ULA_SOURCE_1[2:0]), .out(shifter_2_out));
  Comparator #(.mode("unsigned")) comparator_1 (
    .a(ULA_SOURCE_2), .b(ULA_SOURCE_1), .gt(ULA_UNSIGNED_GREATER), .eq(ULA_EQUAL));  // open: lt
  Comparator comparator_2 (.a(ULA_SOURCE_2), .b(ULA_SOURCE_1), .gt(ULA_SIGNED_GREATER));  // open: eq, lt
  Multiplexer #(.select(3), .width(8), .enable("false")) multiplexer_1 (
    .in0(and_1_out), .in1(or_1_out), .in2(adder_1_out), .in3(shifter_1_out), .in4(shifter_2_out),
    .in5({ULA_SOURCE_2[7:2], ULA_SOURCE_1[1:0]}), .out(ULA_OUT), .sel(ULA_OPCODE));  // open: in6, in7
endmodule

module BREG (
  input  BREG_CLEAR,
  input  [7:0] BREG_RX,
  input  BREG_CLOCK,
  input  BREG_WEN,
  input  [1:0] BREG_SELECT_1,
  input  [1:0] BREG_SELECT_2,
  output [7:0] BREG_OUT1,
  output [7:0] BREG_OUT2
);

  wire decoder_1_out0, decoder_1_out1, decoder_1_out2, decoder_1_out3;
  wire [7:0] BREG_R1_q, BREG_R2_q, BREG_R3_q, BREG_SP_q;

  Decoder #(.select(2), .disabled(0)) decoder_1 (
    .out0(decoder_1_out0), .out1(decoder_1_out1), .out2(decoder_1_out2), .out3(decoder_1_out3),
    .sel(BREG_SELECT_1), .en(BREG_WEN));
  Register BREG_SP (.D(BREG_RX), .en(decoder_1_out0), .Q(BREG_SP_q), .clk(BREG_CLOCK), .clr(BREG_CLEAR));
  Register BREG_R1 (.D(BREG_RX), .en(decoder_1_out1), .Q(BREG_R1_q), .clk(BREG_CLOCK), .clr(BREG_CLEAR));
  Register BREG_R2 (.D(BREG_RX), .en(decoder_1_out2), .Q(BREG_R2_q), .clk(BREG_CLOCK), .clr(BREG_CLEAR));
  Register BREG_R3 (.D(BREG_RX), .en(decoder_1_out3), .Q(BREG_R3_q), .clk(BREG_CLOCK), .clr(BREG_CLEAR));
  Multiplexer #(.select(2), .width(8), .enable("false")) multiplexer_1 (
    .in0(BREG_SP_q), .in1(BREG_R1_q), .in2(BREG_R2_q), .in3(BREG_R3_q), .out(BREG_OUT1), .sel(BREG_SELECT_1));
  Multiplexer #(.select(2), .width(8), .enable("false")) multiplexer_2 (
    .in0(BREG_SP_q), .in1(BREG_R1_q), .in2(BREG_R2_q), .in3(BREG_R3_q), .out(BREG_OUT2), .sel(BREG_SELECT_2));
endmodule

module INSTR_MEM (
  input  [7:0] INSTR_MEM_ADDR,
  input  INSTR_MEM_CLEAR,
  output [7:0] INSTR_MEM_OUT
);

  RAM ram_1 (.addr(INSTR_MEM_ADDR), .data(INSTR_MEM_OUT), .sel(1'b1), .ld(1'b1), .clr(INSTR_MEM_CLEAR));  // open: clk
endmodule

module DATA_MEM (
  input  [7:0] DATA_MEM_ADDR,
  input  DATA_MEM_CLOCK,
  input  DATA_MEM_CLEAR,
  input  [7:0] DATA_MEM_DATA,
  input  DATA_MEM_WEN,
  output [7:0] DATA_MEM_OUT
);

  RAM #(.bus("separate")) ram_1 (
    .addr(DATA_MEM_ADDR), .din(DATA_MEM_DATA), .data(DATA_MEM_OUT), .str(DATA_MEM_WEN), .sel(1'b1),
    .clk(DATA_MEM_CLOCK), .ld(1'b1), .clr(DATA_MEM_CLEAR));
endmodule

module CPU (
);

  wire CPU_CLOCK, CTL_BREG_WRITE_ENABLE, CTL_BREG_WRITE_SOURCE, CTL_DATA_MEM_WRITE_ENABLE,
       ctl_jump_1_ctl_jump, CTL_PC_SELECT, CTL_PC_SELECT_ENABLE, CTL_ULA_SOURCE_2, not_1_out,
       SR_sr_carry_out, SR_sr_equal_out, SR_sr_signed_greater_out, SR_sr_unsigned_greater_out, ULA_CARRY,
       ULA_EQUAL, ULA_SIGNED_GREATER, ULA_UNSIGNED_GREATER;
  wire [1:0] CTL_ULA_SOURCE_1, INSTR_NUM_2BITS;
  wire [2:0] CTL_ULA_OPCODE;
  wire [3:0] INSTR_OPCODE;
  wire [3:2] INSTR_NUM_4BITS;
  wire [7:0] bit_extender_1_out, bit_extender_2_out, BREG_RX, BREG_RY, DATA_MEM_OUT, multiplexer_1_out,
       multiplexer_2_out, multiplexer_3_out, multiplexer_4_out, PC, ULA_OUT;

  Clock u_CPU_CLOCK (.out(CPU_CLOCK));
  Multiplexer #(.width(8), .enable("false")) multiplexer_1 (
    .in0(ULA_OUT), .in1(DATA_MEM_OUT), .out(multiplexer_1_out), .sel(CTL_BREG_WRITE_SOURCE));
  Multiplexer #(.width(8), .enable("false")) multiplexer_2 (
    .in0(ULA_OUT), .in1(BREG_RX), .out(multiplexer_2_out), .sel(CTL_PC_SELECT));
  not not_1 (not_1_out, CTL_PC_SELECT_ENABLE);
  Counter counter_1 (
    .load(CTL_PC_SELECT_ENABLE), .D(multiplexer_2_out), .count(not_1_out), .Q(PC), .clk(CPU_CLOCK));  // open: carry, clr
  assign bit_extender_1_out = {{6{1'b0}}, INSTR_NUM_2BITS};  // Bit_Extender bit_extender_1
  assign bit_extender_2_out = {{4{1'b0}}, {INSTR_NUM_4BITS, INSTR_NUM_2BITS}};  // Bit_Extender bit_extender_2
  INSTR_MEM Instruction_Memory (
    .INSTR_MEM_ADDR(PC), .INSTR_MEM_OUT({INSTR_NUM_4BITS, INSTR_NUM_2BITS, INSTR_OPCODE}));  // open: INSTR_MEM_CLEAR
  Multiplexer #(.width(8), .enable("false")) multiplexer_3 (
    .in0(BREG_RY), .in1(PC), .out(multiplexer_3_out), .sel(CTL_ULA_SOURCE_2));
  Multiplexer #(.select(2), .width(8), .enable("false")) multiplexer_4 (
    .in0(BREG_RX), .in1(bit_extender_1_out), .in2(bit_extender_2_out), .out(multiplexer_4_out),
    .sel(CTL_ULA_SOURCE_1));  // open: in3
  BREG Registers (
    .BREG_RX(multiplexer_1_out), .BREG_CLOCK(CPU_CLOCK), .BREG_WEN(CTL_BREG_WRITE_ENABLE),
    .BREG_SELECT_1(INSTR_NUM_4BITS), .BREG_SELECT_2(INSTR_NUM_2BITS), .BREG_OUT1(BREG_RY), .BREG_OUT2(BREG_RX));  // open: BREG_CLEAR
  ULA ALU (
    .ULA_SOURCE_2(multiplexer_3_out), .ULA_SOURCE_1(multiplexer_4_out), .ULA_OPCODE(CTL_ULA_OPCODE),
    .ULA_OUT(ULA_OUT), .ULA_CARRY(ULA_CARRY), .ULA_UNSIGNED_GREATER(ULA_UNSIGNED_GREATER),
    .ULA_SIGNED_GREATER(ULA_SIGNED_GREATER), .ULA_EQUAL(ULA_EQUAL));
  SR SR (
    .SR_CARRY(ULA_CARRY), .SR_UNSIGNED_GREATER(ULA_UNSIGNED_GREATER), .SR_SIGNED_GREATER(ULA_SIGNED_GREATER),
    .SR_EQUAL(ULA_EQUAL), .SR_CARRY_OUT(SR_sr_carry_out),
    .SR_UNSIGNED_GREATER_OUT(SR_sr_unsigned_greater_out), .SR_SIGNED_GREATER_OUT(SR_sr_signed_greater_out),
    .SR_EQUAL_OUT(SR_sr_equal_out));  // open: SR_CLOCK
  CTL_JUMP ctl_jump_1 (
    .CTL_OPCODE(INSTR_OPCODE), .CTL_CARRY(SR_sr_carry_out),
    .CTL_UNSIGNED_GREATER(SR_sr_unsigned_greater_out), .CTL_SIGNED_GREATER(SR_sr_signed_greater_out),
    .CTL_EQUAL(SR_sr_equal_out), .CTL_JUMP(ctl_jump_1_ctl_jump));
  DATA_MEM Data_memory (
    .DATA_MEM_ADDR(BREG_RX), .DATA_MEM_CLOCK(CPU_CLOCK), .DATA_MEM_DATA(BREG_RY),
    .DATA_MEM_WEN(CTL_DATA_MEM_WRITE_ENABLE), .DATA_MEM_OUT(DATA_MEM_OUT));  // open: DATA_MEM_CLEAR
  CONTROL control_1 (
    .CTL_OPCODE(INSTR_OPCODE), .CTL_JUMP(ctl_jump_1_ctl_jump),
    .CTL_DATA_MEM_WRITE_ENABLE(CTL_DATA_MEM_WRITE_ENABLE), .CTL_BREG_WRITE_SOURCE(CTL_BREG_WRITE_SOURCE),
    .CTL_BREG_WRITE_ENABLE(CTL_BREG_WRITE_ENABLE), .CTL_ULA_SOURCE_2(CTL_ULA_SOURCE_2),
    .CTL_ULA_SOURCE_1(CTL_ULA_SOURCE_1), .CTL_ULA_OPCODE(CTL_ULA_OPCODE),
    .CTL_PC_SELECT_ENABLE(CTL_PC_SELECT_ENABLE), .CTL_PC_SELECT(CTL_PC_SELECT));

  // Other names for the same wires on the sheet: INSTR_NUM_4BITS[1:0] = INSTR_NUM_2BITS;
  //   INSTR_RX[1:0] = INSTR_NUM_2BITS; INSTR_RY[1:0] = INSTR_NUM_4BITS
endmodule

module CONTROL (
  input  [3:0] CTL_OPCODE,
  input  CTL_JUMP,
  output CTL_DATA_MEM_WRITE_ENABLE,
  output CTL_BREG_WRITE_SOURCE,
  output CTL_BREG_WRITE_ENABLE,
  output CTL_ULA_SOURCE_2,
  output [1:0] CTL_ULA_SOURCE_1,
  output [2:0] CTL_ULA_OPCODE,
  output CTL_PC_SELECT_ENABLE,
  output CTL_PC_SELECT
);

  wire decoder_1_out0, decoder_1_out3, decoder_1_out4, decoder_1_out5, decoder_1_out6, decoder_1_out7,
       decoder_1_out8;

  Decoder #(.select(4), .disabled(0), .enable("false")) decoder_1 (
    .out0(decoder_1_out0), .out1(CTL_DATA_MEM_WRITE_ENABLE), .out3(decoder_1_out3), .out4(decoder_1_out4),
    .out5(decoder_1_out5), .out6(decoder_1_out6), .out7(decoder_1_out7), .out8(decoder_1_out8),
    .out10(CTL_BREG_WRITE_SOURCE), .out15(CTL_PC_SELECT), .sel(CTL_OPCODE));  // open: out2, out9, out11, out12, out13, out14
  nor nor_1 (CTL_BREG_WRITE_ENABLE, CTL_DATA_MEM_WRITE_ENABLE, CTL_PC_SELECT, decoder_1_out0, CTL_JUMP);
  or or_1 (CTL_ULA_SOURCE_1[0], decoder_1_out3, decoder_1_out5, decoder_1_out4);
  or or_2 (CTL_ULA_OPCODE[0], decoder_1_out3, decoder_1_out7, decoder_1_out4);
  or or_3 (CTL_ULA_OPCODE[1], decoder_1_out4, CTL_JUMP, decoder_1_out8);
  or or_4 (CTL_ULA_OPCODE[2], decoder_1_out5, decoder_1_out3);
  or or_5 (CTL_PC_SELECT_ENABLE, CTL_JUMP, CTL_PC_SELECT);

  assign CTL_ULA_SOURCE_1[1] = CTL_JUMP;
  assign CTL_ULA_SOURCE_2 = CTL_JUMP;
endmodule

module SR (
  input  SR_CLOCK,
  input  SR_CARRY,
  input  SR_UNSIGNED_GREATER,
  input  SR_SIGNED_GREATER,
  input  SR_EQUAL,
  output SR_CARRY_OUT,
  output SR_UNSIGNED_GREATER_OUT,
  output SR_SIGNED_GREATER_OUT,
  output SR_EQUAL_OUT
);

  D_Flip_Flop d_ff_1 (.clk(SR_CLOCK), .D(SR_CARRY), .Q(SR_CARRY_OUT), .en(1'b1));  // open: Qn, preset, reset
  D_Flip_Flop d_ff_2 (
    .clk(SR_CLOCK), .D(SR_UNSIGNED_GREATER), .Q(SR_UNSIGNED_GREATER_OUT), .en(1'b1));  // open: Qn, preset, reset
  D_Flip_Flop d_ff_3 (.clk(SR_CLOCK), .D(SR_SIGNED_GREATER), .Q(SR_SIGNED_GREATER_OUT));  // open: Qn, preset, en, reset
  D_Flip_Flop d_ff_4 (.clk(SR_CLOCK), .D(SR_EQUAL), .Q(SR_EQUAL_OUT), .en(1'b1));  // open: Qn, preset, reset
endmodule

module CTL_JUMP (
  input  [3:0] CTL_OPCODE,
  input  CTL_CARRY,
  input  CTL_UNSIGNED_GREATER,
  input  CTL_SIGNED_GREATER,
  input  CTL_EQUAL,
  output CTL_JUMP
);

  wire and_2_out, and_3_out, decoder_1_out11, decoder_1_out12, decoder_1_out13, decoder_1_out14;

  Decoder #(.select(4)) decoder_1 (
    .out11(decoder_1_out11), .out12(decoder_1_out12), .out13(decoder_1_out13), .out14(decoder_1_out14),
    .sel(CTL_OPCODE));  // open: out0, out1, out2, out3, out4, out5, out6, out7, out8, out9, out10, out15, en
  // AND_Gate and_1 has open pins: in0=decoder_1_out12, in1=CTL_EQUAL, out=open
  and and_2 (and_2_out, decoder_1_out13, CTL_SIGNED_GREATER);
  and and_3 (and_3_out, decoder_1_out14, CTL_CARRY);
  or or_1 (CTL_JUMP, decoder_1_out11, and_2_out, and_3_out);
endmodule
